# Fritzing sketch project (saved by Fritzing 0.9.0b)

parts:
  Part2 = DFRobot Shield  # not connected
  Part3 = Troyka Shield
  Part4 = Troyka Shield  # not connected
  Part5 = DFRobot Shield  # not connected
  Part6 = Troyka Shield  # not connected
  Part7 = DFRobot Shield
  Part8 = Troyka Shield
  Part9 = DFRobot Shield
  Part10 = Arduino Uno (Rev3)
  Part11 = Arduino Uno (Rev3)  # not connected
  Part12 = Arduino Uno (Rev3)
  Part13 = Arduino Uno (Rev3)
  J1 = Infrared Proximity Sensor  # not connected
  J2 = Infrared Proximity Sensor  # not connected
  J3 = Infrared Proximity Sensor  # not connected
  J4 = Infrared Proximity Sensor  # not connected
  J5 = Infrared Proximity Sensor  # not connected
  J6 = Infrared Proximity Sensor  # not connected
  J7 = Infrared Proximity Sensor  # not connected
  J8 = Infrared Proximity Sensor  # not connected
  VCC1 = Battery block 9V

nets:
  N1: Part3.AREF, Part12.AREF
  GND: Part3.GND, Part12.GND
  N2: Part3.13, Part12.D13/SCK
  N3: Part3.12, Part12.D12/MISO
  N4: Part3.11, Part12.D11_PWM/MOSI
  N5: Part3.10, Part12.D10_PWM/SS
  N6: Part3.9, Part12.D9_PWM
  N7: Part3.8, Part12.D8
  N8: Part3.7, Part12.D7
  N9: Part3.6, Part12.D6_PWM
  N10: Part3.5, Part12.D5_PWM
  N11: Part3.4, Part12.D4
  N12: Part3.3, Part12.D3_PWM
  N13: Part3.2, Part12.D2
  N14: Part3.1, Part12.D1/TX
  N15: Part3.0, Part12.D0/RX
  N16: Part3.A5, Part12.A5/SCL
  N17: Part3.A4, Part12.A4/SDA
  N18: Part3.A3, Part12.A3
  N19: Part3.A2, Part12.A2
  N20: Part3.A1, Part12.A1
  N21: Part3.A0, Part12.A0
  VIN: Part3.Vin, Part12.VIN
  5V: Part3.5V, Part12.5V
  3.3V: Part3.3.3V, Part12.3V3
  N22: Part3.RESET, Part12.RESET
  N23: Part3.IOREF, Part12.ioref
  N24: Part7.RXD, Part13.D0/RX
  N25: Part7.TXD, Part13.D1/TX
  N26: Part7.2, Part13.D2
  N27: Part7.3, Part13.D3_PWM
  N28: Part7.4, Part13.D4
  N29: Part7.5, Part13.D5_PWM
  N30: Part7.6, Part13.D6_PWM
  N31: Part7.7, Part13.D7
  N32: Part7.8, Part13.D8
  N33: Part7.9, Part13.D9_PWM
  N34: Part7.10, Part13.D10_PWM/SS
  N35: Part7.11, Part13.D11_PWM/MOSI
  N36: Part7.12, Part13.D12/MISO
  N37: Part7.13, Part13.D13/SCK
  GND_2: Part7.GND, Part9.GND, Part13.GND
  N38: Part7.AREF, Part13.AREF
  N39: Part7.SDA, Part7.A4, Part13.A4/SDA
  N40: Part7.SCL, Part7.A5, Part13.A5/SCL
  N41: Part7.A3, Part13.A3
  N42: Part7.A2, Part13.A2
  N43: Part7.A1, Part13.A1
  N44: Part7.A0, Part13.A0
  VIN_2: Part7.VIN, Part9.VIN, Part13.VIN
  5V_2: Part7.5V, Part13.5V
  3V3: Part7.3V3, Part13.3V3
  N45: Part7.RST, Part13.RESET
  N46: Part7.IOREF, Part13.ioref
  N47: Part7.A, Part9.A
  N48: Part7.B, Part9.B
  N49: Part8.AREF, Part10.AREF
  GND_3: Part8.GND, Part10.GND, VCC1.-
  N50: Part8.13, Part10.D13/SCK
  N51: Part8.12, Part10.D12/MISO
  N52: Part8.11, Part10.D11_PWM/MOSI
  N53: Part8.10, Part10.D10_PWM/SS
  N54: Part8.9, Part10.D9_PWM
  N55: Part8.8, Part10.D8
  N56: Part8.7, Part10.D7
  N57: Part8.6, Part10.D6_PWM
  N58: Part8.5, Part10.D5_PWM
  N59: Part8.4, Part10.D4
  N60: Part8.3, Part10.D3_PWM
  N61: Part8.2, Part10.D2
  N62: Part8.1, Part10.D1/TX
  N63: Part8.0, Part10.D0/RX
  N64: Part8.A5, Part10.A5/SCL
  N65: Part8.A4, Part10.A4/SDA
  N66: Part8.A3, Part10.A3
  N67: Part8.A2, Part10.A2
  N68: Part8.A1, Part10.A1
  N69: Part8.A0, Part10.A0
  VIN_3: Part8.Vin, Part10.VIN, VCC1.+
  5V_3: Part8.5V, Part10.5V
  3.3V_2: Part8.3.3V, Part10.3V3
  N70: Part8.RESET, Part10.RESET
  N71: Part8.IOREF, Part10.ioref
